# Fritzing sketch circuit (saved by Fritzing 0.9.3b)
breadboards: 1

parts:
  DRV1 = DollaTek DRV8833
  Part1 = GY-BMEP280 Barometric Pressure Sensor - Breakout
  OLED_I2C1 = OLED 128x64 I2C Monochrome Display
  M2 = DFR sen0308 [package=THT]
  M3 = DFR sen0308 [package=THT]
  M1 = DC Motor
  A1 = ESP32-C6 supermini
  Part2 = GY-BMEP280 Barometric Pressure Sensor - Breakout

nets:
  N1: DRV1.pin_2, M1.pin_2
  N2: DRV1.pin_3, M1.pin_1
  N3: DRV1.pin_6, A1.GP18
  N4: DRV1.pin_7, A1.GP19
  N5: DRV1.pin_8, A1.GP20
  N6: DRV1.pin_9, A1.5V
  GND: DRV1.pin_10, Part1.GND, OLED_I2C1.GND, M2.pin1, M2.pin3, M3.pin1, M3.pin3, A1.GND, Part2.GND
  3.3V: Part1.VCC, OLED_I2C1.VDD, M2.pin4, M3.pin4, A1.3V3, Part2.VCC
  N7: Part1.SCL, OLED_I2C1.SCK, A1.GP7
  N8: Part1.SDA, OLED_I2C1.SDA, A1.GP6
  N9: M2.pin2, A1.GP2
  N10: M3.pin2, A1.GP1
  N11: A1.GP8, Part2.SDA
  N12: A1.GP9, Part2.SCL

notes:
  Pinout Definitions
  SCL0 -> 7
  SDA0 -> 6
  SCL1 -> 9
  SDA1 -> 8
  ADC0 -> 0
  ADC1 -> 1
  IN1 -> 19
  IN2 -> 20
  STBY -> 18
  GreenPulse, Smart IoT solution that monitors plant conditions and automates irrigation for efficient water usage., v1.1
  Water pump
  Display
  esp32 c6
  Soil moisture Sensors
  BME 280
  DRV 8833

custom parts:
  DollaTek DRV8833: DollaTek DRV8833 1.5A 2-Channel DC Motor Drive Board
  GY-BMEP280 Barometric Pressure Sensor - Breakout: The BME280 is a chip which was originally designed for the next generation of smartphones. It is made up of a very accurate pressure sensor and an associated temperature sensor which helps calibrate the pressure readings. And just for fun they threw in a pretty solid humidity sensor in there as well! So with an I2C connection you have access to enough weather data to make some pretty good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
  DFR sen0308: This is a new type of waterproof soil moisture sensor introduced by DFRobot. Compared with the previous version of the soil moisture sensor, it has increased waterproof performance, optimized corrosion resistance, increased plate length and optimized circuit performance. Compared with the resistive sensor, the capacitive soil moisture sensor solves the problem that the resistive sensor is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
  ESP32-C6 supermini: TZT SuperMini ESP32-C6 WiFi+Bluetooth ESP32 Development Board.
